# Fritzing sketch SBMSEsp32 (saved by Fritzing 0.9.3b)
breadboards: 1

parts:
  U1 = NodeMCU V1.0
  VCC1 = Battery
  LED1 = LED - 5mm [color="Orange (605nm)" package="5 mm [THT]"]
  KY-1 = Keyes Relay [package=THT]
  R1 = Resistor [tolerance=±5% resistance=330 package=THT]
  S1 = Pushbutton [package="[THT]"]
  R2 = Resistor [tolerance=±5% resistance=220 package=THT]
  LED2 = LED - 5mm [color="Red (633nm)" package="5 mm [THT]"]
  LED3 = LED - 5mm [color="Green (560nm)" package="5 mm [THT]"]
  R3 = Resistor [tolerance=±5% resistance=330 package=THT]
  R4 = Resistor [tolerance=±5% resistance=330 package=THT]
  J1 = shrouded pin header, 16 pins [form="♂ (shrouded male)"]
  LED4 = LED - 5mm [color="Blue (470nm)" package="5 mm [THT]"]
  R5 = Resistor [tolerance=±5% resistance=330 package=THT]
  U2 = Optocoupler [package=THT]

nets (from the breadboard view):
  N1: U1.D0, LED2.anode
  N2: U1.D1, LED3.anode
  N3: U1.D2, KY-1.ground
  N4: U1.D3, LED4.anode
  N5: U1.D5, S1.Pin_1, S1.Pin_2, R2.Pin_0
  N6: U1.D7, U2.Pin_2
  N7: U1.GND, KY-1.power, R2.Pin_1, R3.Pin_1, R4.Pin_1, R5.Pin_1, U2.Pin_1
  N8: U1.3V3, S1.Pin_3, S1.Pin_4, U2.Pin_3
  N9: U1.Vin, KY-1.signal
  N10: VCC1.-, LED1.cathode
  N11: VCC1.+, KY-1.NO
  N12: LED1.anode, R1.Pin_1
  N13: LED2.cathode, R4.Pin_0
  N14: LED3.cathode, R3.Pin_0
  N15: J1.pin1, U2.Pin_5
  N16: J1.pin12, U2.Pin_6
  N17: LED4.cathode, R5.Pin_0

notes:
  TX/GND SBMS
  5V vom USB
  SBMS Überwachung
  Optocoupler 3.3v auf 3.3v
  3-Farb-LED, hier dar-gestellt durch 3 LED
  LED stellt Verbraucher (Inverter) dar
  GND
  TX->RC
  RC

custom parts:
  NodeMCU V1.0: ESP8266 based NodeMCU
  Keyes Relay: The Keyes 5V relay module is suitable for SCM development, home appliance control. It uses a 5V~12V TIL control signal which can control DC / AC signal.
